# Fritzing sketch LED_Matrix_v0 (saved by Fritzing 0.9.3b)
circuit board: 4.89108cm x 5.15388cm

parts:
  part = Power plug  # not connected
  Arduino_NANO = Arduino Nano (Rev3.0)
  I2C_Magnetic_Connector = Header 4 [package=molex-1x4_lock]
  RGB_SMD_LED_-_MATRIX = SMD RGB LED (WS2812) [package=5050]

nets:
  GND: Arduino_NANO.GND, I2C_Magnetic_Connector.4, RGB_SMD_LED_-_MATRIX.VSS
  N1: Arduino_NANO.D11/MOSI, RGB_SMD_LED_-_MATRIX.DIn
  5V: Arduino_NANO.5V, I2C_Magnetic_Connector.1, RGB_SMD_LED_-_MATRIX.VCC
  N2: Arduino_NANO.A5, I2C_Magnetic_Connector.3
  N3: Arduino_NANO.A4, I2C_Magnetic_Connector.2

notes:
  Connect this to any I2C device (i.e. Raspberry Pi) :
  1: 5V
  2: Data
  3: Clk
  4: GND
