# Fritzing sketch XY_Stage_v0 (saved by Fritzing 0.9.3b)
circuit board: 4.89108cm x 5.15388cm
breadboards: 1

parts:
  X-Direction = Stepper Motor - Bipolar
  Power_plug1 = Power plug  # not connected
  part = Power plug  # not connected
  Arduino_NANO = Arduino Nano (Rev3.0)
  L294 = L293D [package=THT]
  L295 = L293D [package=THT]
  Y-Direction = Stepper Motor - Bipolar

nets:
  N1: X-Direction.A, L294.Out_1_(_Controlled_by_Enable_1_)
  N2: X-Direction.C, L294.Out_2_(_Controlled_by_Enable_1_)
  N3: X-Direction.B, L294.Out_4_(_Controlled_by_Enable_2_)
  N4: X-Direction.D, L294.Out_3_(_Controlled_by_Enable_2_)
  N5: Arduino_NANO.D2, L294.In_1
  N6: Arduino_NANO.D3, L294.In_2
  N7: Arduino_NANO.D4, L294.In_3
  N8: Arduino_NANO.D5, L294.In_4
  N9: Arduino_NANO.D6, L295.In_1
  N10: Arduino_NANO.D7, L295.In_2
  N11: Arduino_NANO.D8, L295.In_3
  N12: Arduino_NANO.D9, L295.In_4
  N13: Arduino_NANO.GND, L294.0V, L295.0V
  N14: Arduino_NANO.5V, L294.+Vmotor, L294.+V, L295.+Vmotor, L295.+V
  N15: L295.Out_1_(_Controlled_by_Enable_1_), Y-Direction.A
  N16: L295.Out_2_(_Controlled_by_Enable_1_), Y-Direction.C
  N17: L295.Out_3_(_Controlled_by_Enable_2_), Y-Direction.D
  N18: L295.Out_4_(_Controlled_by_Enable_2_), Y-Direction.B

notes:
  The motor used in this example is a salvaged cd-rom stepper. You can identify it because it is attached to a "serpentine". The schematic is based on this very simple yet functional one.
  http://blog.whattomake.co.kr/158
  It works very well with the examples library of Arduino environment.
  You can use the +5v from arduino board or an external supply if you need more voltage.
