# Fritzing sketch Z_Stage_ESP_v0 (saved by Fritzing 0.9.3b)
circuit board: 4.89108cm x 5.15388cm
breadboards: 1

parts:
  Z-Direction_(Objective) = Stepper Motor - Bipolar
  Z-Direction_(Sample) = Stepper Motor - Bipolar
  U2 = ESP8266 WiFi Module [part_number=ESP8266]
  IC1 = ULN2003A [package="SO16 [SMD]"]
  IC3 = ULN2003A [package="SO16 [SMD]"]
  JP1 = Header 1 [package=1x01_offset]
  JP2 = Header 1 [package=1x01_offset]

nets:
  N1: Z-Direction_(Objective).A, IC1.Out_1
  N2: Z-Direction_(Objective).C, IC1.Out_2
  N3: Z-Direction_(Objective).B, IC1.Out_4
  N4: Z-Direction_(Objective).D, IC1.Out_5
  N5: Z-Direction_(Sample).A, IC3.Out_1
  N6: Z-Direction_(Sample).C, IC3.Out_2
  N7: Z-Direction_(Sample).B, IC3.Out_4
  N8: Z-Direction_(Sample).D, IC3.Out_5
  N9: U2.D2, IC1.In_3
  N10: U2.D0, IC1.In_1
  N11: U2.D1, IC1.In_2
  N12: U2.D3, IC1.In_4
  N13: U2.IO4, IC3.In_1
  N14: U2.3.3V, IC1.0V, IC3.0V
  N15: U2.GND, IC1.COM_-_Common, IC3.COM_-_Common
  N16: U2.IO5, IC3.In_2
  N17: U2.IO12, IC3.In_3
  N18: U2.IO13, IC3.In_4
  N19: IC1.Out_3, JP1.1
  N20: IC3.Out_3, JP2.1

notes:
  The motor used in this example is a salvaged cd-rom stepper. You can identify it because it is attached to a "serpentine". The schematic is based on this very simple yet functional one.
  http://blog.whattomake.co.kr/158
  It works very well with the examples library of Arduino environment.
  You can use the +5v from arduino board or an external supply if you need more voltage.
  13|12|14|27
  26|25|23|22
